// Logisim project LPE1_2003127_Q1.circ as structural Verilog: 1 circuit, main circuit main
module main (
  input  M,
  input  P,
  input  Q,
  output out_4
);

  wire nand_1_out, not_1_out;

  not not_1 (not_1_out, M);
  nand nand_1 (nand_1_out, P, Q);
  or or_1 (out_4, not_1_out, nand_1_out);

  // Notes on the sheet:
  //   O
endmodule
